# Fritzing sketch BreadboardDiagram (saved by Fritzing 0.9.4)
breadboards: 1

parts:
  Part1 = Arduino Mega 2560 (Rev3)
  IC1 = L293D [package=THT]
  U1 = SLIDER [package=slider]
  M1 = DC Motor

nets:
  N1: Part1.A0, U1.S
  N2: Part1.GND, IC1.0V, U1.E
  N3: Part1.D13_PWM, IC1.In_1
  N4: Part1.D11_PWM, IC1.In_2
  N5: Part1.5V, IC1.+Vmotor, U1.A
  N6: IC1.Out_1_(_Controlled_by_Enable_1_), M1.pin_1
  N7: IC1.Out_2_(_Controlled_by_Enable_1_), M1.pin_2
